// Logisim project parcial2_mejorado.circ as structural Verilog: 4 circuits, main circuit contador
module main (
  input  in_1,
  input  in_2,
  input  in_3,
  input  in_4,
  input  in_5,
  input  in_6,
  input  in_7,
  input  in_8
);

  wire comparar_1_x, contador_1_a_2, contador_1_b_2, contador_1_c_2, contador_2_a_2, contador_2_b_2,
       contador_2_c_2, n7_hex_1_a_2, n7_hex_1_b_2, n7_hex_1_c_2, n7_hex_1_d_2, n7_hex_1_e, n7_hex_1_f,
       n7_hex_1_g, n7_hex_2_a_2, n7_hex_2_b_2, n7_hex_2_c_2, n7_hex_2_d_2, n7_hex_2_e, n7_hex_2_f,
       n7_hex_2_g, not_1_out;

  comparar comparar_1 (
    .A(in_1), .B(in_2), .C(in_3), .D(in_4), .E(in_5), .F(in_6), .G(in_7), .H(in_8), .x(comparar_1_x));
  contador contador_1 (
    .A(in_4), .B(in_3), .C(in_2), .D(in_1), .a_2(contador_1_a_2), .b_2(contador_1_b_2), .c_2(contador_1_c_2));
  contador contador_2 (
    .A(in_8), .B(in_7), .C(in_6), .D(in_5), .a_2(contador_2_a_2), .b_2(contador_2_b_2), .c_2(contador_2_c_2));
  _7_hex u_7_hex_1 (
    .A(1'b0), .B(contador_1_a_2), .C(contador_1_b_2), .D(contador_1_c_2), .a_2(n7_hex_1_a_2),
    .b_2(n7_hex_1_b_2), .c_2(n7_hex_1_c_2), .d_2(n7_hex_1_d_2), .e(n7_hex_1_e), .f(n7_hex_1_f), .g(n7_hex_1_g));
  _7_hex u_7_hex_2 (
    .A(1'b0), .B(contador_2_a_2), .C(contador_2_b_2), .D(contador_2_c_2), .a_2(n7_hex_2_a_2),
    .b_2(n7_hex_2_b_2), .c_2(n7_hex_2_c_2), .d_2(n7_hex_2_d_2), .e(n7_hex_2_e), .f(n7_hex_2_f), .g(n7_hex_2_g));
  LED S (.in(not_1_out));
  LED N (.in(not_1_out));
  not not_1 (not_1_out, comparar_1_x);
  LED O (.in(comparar_1_x));
  LED E (.in(comparar_1_x));
  _7_Segment_Display u_7_segment_display_1 (
    .g(n7_hex_1_g), .f(n7_hex_1_f), .a(n7_hex_1_a_2), .b(n7_hex_1_b_2), .e(n7_hex_1_e), .d(n7_hex_1_d_2),
    .c(n7_hex_1_c_2));  // open: dp
  _7_Segment_Display u_7_segment_display_2 (
    .g(n7_hex_2_g), .f(n7_hex_2_f), .a(n7_hex_2_a_2), .b(n7_hex_2_b_2), .e(n7_hex_2_e), .d(n7_hex_2_d_2),
    .c(n7_hex_2_c_2));  // open: dp
endmodule

module contador (
  input  A,
  input  B,
  input  C,
  input  D,
  output a_2,
  output b_2,
  output c_2
);

  wire and_2_out, and_3_out, and_4_out, and_5_out, and_6_out, and_7_out, and_8_out, and_9_out, and_10_out,
       and_11_out, and_12_out, and_13_out, and_14_out, and_15_out, and_16_out, not_1_out, not_2_out,
       not_3_out, not_4_out, not_5_out, not_6_out, not_7_out, not_8_out, not_9_out, not_10_out, not_11_out,
       not_12_out, not_13_out, not_14_out, not_15_out, not_16_out, not_17_out, not_18_out, not_19_out,
       not_20_out, not_21_out, not_22_out, not_23_out;

  and and_1 (a_2, A, B, C, D);
  not not_1 (not_1_out, A);
  and and_2 (and_2_out, not_1_out, C, D);
  not not_2 (not_2_out, A);
  and and_3 (and_3_out, not_2_out, B, D);
  not not_3 (not_3_out, A);
  and and_4 (and_4_out, not_3_out, B, C);
  not not_4 (not_4_out, B);
  and and_5 (and_5_out, A, not_4_out, D);
  and and_6 (and_6_out, A, not_5_out, C);
  not not_5 (not_5_out, B);
  and and_7 (and_7_out, A, B, not_6_out);
  not not_6 (not_6_out, C);
  and and_8 (and_8_out, A, B, not_7_out);
  not not_7 (not_7_out, D);
  not not_8 (not_8_out, A);
  not not_9 (not_9_out, B);
  not not_10 (not_10_out, C);
  not not_11 (not_11_out, A);
  not not_12 (not_12_out, B);
  not not_13 (not_13_out, D);
  not not_14 (not_14_out, A);
  not not_15 (not_15_out, C);
  not not_16 (not_16_out, D);
  not not_17 (not_17_out, A);
  not not_18 (not_18_out, B);
  not not_19 (not_19_out, C);
  not not_20 (not_20_out, D);
  not not_21 (not_21_out, B);
  not not_22 (not_22_out, C);
  not not_23 (not_23_out, D);
  and and_9 (and_9_out, not_8_out, not_9_out, not_10_out, D);
  and and_10 (and_10_out, not_11_out, not_12_out, C, not_13_out);
  and and_11 (and_11_out, not_14_out, B, not_15_out, not_16_out);
  and and_12 (and_12_out, not_17_out, B, C, D);
  and and_13 (and_13_out, A, not_18_out, not_19_out, not_20_out);
  and and_14 (and_14_out, A, not_21_out, C, D);
  and and_15 (and_15_out, A, B, not_22_out, D);
  and and_16 (and_16_out, A, B, C, not_23_out);
  or or_1 (b_2, and_2_out, and_3_out, and_4_out, and_5_out, and_6_out, and_7_out, and_8_out);
  or or_2 (c_2, and_9_out, and_10_out, and_11_out, and_12_out, and_13_out, and_14_out, and_15_out, and_16_out);
endmodule

module comparar (
  input  A,
  input  B,
  input  C,
  input  D,
  input  E,
  input  F,
  input  G,
  input  H,
  output x
);

  wire and_1_out, and_2_out, and_3_out, and_4_out, and_5_out, and_6_out, and_7_out, and_8_out, and_9_out,
       and_10_out, and_11_out, and_12_out, and_13_out, and_14_out, and_15_out, and_16_out, and_17_out,
       and_18_out, and_19_out, and_20_out, and_21_out, and_22_out, and_23_out, and_24_out, and_25_out,
       and_26_out, and_27_out, and_28_out, and_29_out, and_30_out, and_31_out, and_32_out, and_33_out,
       and_34_out, and_35_out, and_36_out, and_37_out, and_38_out, and_39_out, and_40_out, and_41_out,
       and_42_out, and_43_out, and_44_out, and_45_out, and_46_out, and_47_out, and_48_out, and_49_out,
       and_50_out, and_51_out, and_52_out, and_53_out, and_54_out, and_55_out, and_56_out, not_1_out,
       not_2_out, not_3_out, not_4_out, not_5_out, not_6_out, not_7_out, not_8_out, not_9_out, not_10_out,
       not_11_out, not_12_out, not_13_out, not_14_out, not_15_out, not_16_out, not_17_out, not_18_out,
       not_19_out, not_20_out, not_21_out, not_22_out, not_23_out, not_24_out, not_25_out, not_26_out,
       not_27_out, not_28_out, not_29_out, not_30_out, not_31_out, not_32_out, not_33_out, not_34_out,
       not_35_out, not_36_out, not_37_out, not_38_out, not_39_out, not_40_out, not_41_out, not_42_out,
       not_43_out, not_44_out, not_45_out, not_46_out, not_47_out, not_48_out, not_49_out, not_50_out,
       not_51_out, not_52_out, not_53_out, not_54_out, not_55_out, not_56_out, not_57_out, not_58_out,
       not_59_out, not_60_out, not_61_out, not_62_out, not_63_out, not_64_out, not_65_out, not_66_out,
       not_67_out, not_68_out, not_69_out, not_70_out, not_71_out, not_72_out, not_73_out, not_74_out,
       not_75_out, not_76_out, not_77_out, not_78_out, not_79_out, not_80_out, not_81_out, not_82_out,
       not_83_out, not_84_out, not_85_out, not_86_out, not_87_out, not_88_out, not_89_out, not_90_out,
       not_91_out, not_92_out, not_93_out, not_94_out, not_95_out, not_96_out, not_97_out, not_98_out,
       not_99_out, not_100_out, not_101_out, not_102_out, not_103_out, not_104_out, not_105_out, not_106_out,
       not_107_out, not_108_out, not_109_out, not_110_out, not_111_out, not_112_out, not_113_out,
       not_114_out, not_115_out, not_116_out, not_117_out, not_118_out, not_119_out, not_120_out,
       not_121_out, not_122_out, not_123_out, not_124_out, not_125_out, not_126_out, not_127_out,
       not_128_out, not_129_out, not_130_out, not_131_out, not_132_out, not_133_out, not_134_out,
       not_135_out, not_136_out, not_137_out, not_138_out, not_139_out, not_140_out, or_1_out, or_2_out;

  not not_1 (not_1_out, A);
  not not_2 (not_2_out, B);
  not not_3 (not_3_out, C);
  not not_4 (not_4_out, D);
  not not_5 (not_5_out, A);
  not not_6 (not_6_out, B);
  not not_7 (not_7_out, C);
  not not_8 (not_8_out, D);
  not not_9 (not_9_out, A);
  not not_10 (not_10_out, B);
  not not_11 (not_11_out, C);
  not not_12 (not_12_out, A);
  not not_13 (not_13_out, B);
  not not_14 (not_14_out, D);
  not not_15 (not_15_out, A);
  not not_16 (not_16_out, C);
  not not_17 (not_17_out, D);
  not not_18 (not_18_out, B);
  not not_19 (not_19_out, C);
  not not_20 (not_20_out, D);
  not not_21 (not_21_out, A);
  not not_22 (not_22_out, B);
  not not_23 (not_23_out, C);
  not not_24 (not_24_out, D);
  not not_25 (not_25_out, A);
  not not_26 (not_26_out, B);
  not not_27 (not_27_out, C);
  not not_28 (not_28_out, A);
  not not_29 (not_29_out, B);
  not not_30 (not_30_out, D);
  not not_31 (not_31_out, A);
  not not_32 (not_32_out, C);
  not not_33 (not_33_out, D);
  not not_34 (not_34_out, B);
  not not_35 (not_35_out, C);
  not not_36 (not_36_out, D);
  not not_37 (not_37_out, A);
  not not_38 (not_38_out, B);
  not not_39 (not_39_out, C);
  not not_40 (not_40_out, A);
  not not_41 (not_41_out, B);
  not not_42 (not_42_out, D);
  not not_43 (not_43_out, A);
  not not_44 (not_44_out, C);
  not not_45 (not_45_out, D);
  not not_46 (not_46_out, B);
  not not_47 (not_47_out, C);
  not not_48 (not_48_out, D);
  not not_49 (not_49_out, A);
  not not_50 (not_50_out, B);
  not not_51 (not_51_out, A);
  not not_52 (not_52_out, C);
  not not_53 (not_53_out, A);
  not not_54 (not_54_out, D);
  not not_55 (not_55_out, B);
  not not_56 (not_56_out, C);
  not not_57 (not_57_out, B);
  not not_58 (not_58_out, D);
  not not_59 (not_59_out, C);
  not not_60 (not_60_out, D);
  not not_61 (not_61_out, A);
  not not_62 (not_62_out, B);
  not not_63 (not_63_out, C);
  not not_64 (not_64_out, D);
  not not_65 (not_65_out, A);
  not not_66 (not_66_out, B);
  not not_67 (not_67_out, C);
  not not_68 (not_68_out, A);
  not not_69 (not_69_out, B);
  not not_70 (not_70_out, D);
  not not_71 (not_71_out, A);
  not not_72 (not_72_out, C);
  not not_73 (not_73_out, D);
  not not_74 (not_74_out, B);
  not not_75 (not_75_out, C);
  not not_76 (not_76_out, D);
  not not_77 (not_77_out, A);
  not not_78 (not_78_out, B);
  not not_79 (not_79_out, C);
  not not_80 (not_80_out, A);
  not not_81 (not_81_out, B);
  not not_82 (not_82_out, D);
  not not_83 (not_83_out, A);
  not not_84 (not_84_out, C);
  not not_85 (not_85_out, D);
  not not_86 (not_86_out, B);
  not not_87 (not_87_out, C);
  not not_88 (not_88_out, D);
  not not_89 (not_89_out, A);
  not not_90 (not_90_out, B);
  not not_91 (not_91_out, A);
  not not_92 (not_92_out, C);
  not not_93 (not_93_out, A);
  not not_94 (not_94_out, D);
  not not_95 (not_95_out, B);
  not not_96 (not_96_out, C);
  not not_97 (not_97_out, B);
  not not_98 (not_98_out, D);
  not not_99 (not_99_out, C);
  not not_100 (not_100_out, D);
  not not_101 (not_101_out, A);
  not not_102 (not_102_out, B);
  not not_103 (not_103_out, C);
  not not_104 (not_104_out, A);
  not not_105 (not_105_out, B);
  not not_106 (not_106_out, D);
  not not_107 (not_107_out, A);
  not not_108 (not_108_out, C);
  not not_109 (not_109_out, D);
  not not_110 (not_110_out, B);
  not not_111 (not_111_out, C);
  not not_112 (not_112_out, D);
  not not_113 (not_113_out, A);
  not not_114 (not_114_out, B);
  not not_115 (not_115_out, A);
  not not_116 (not_116_out, C);
  not not_117 (not_117_out, A);
  not not_118 (not_118_out, D);
  not not_119 (not_119_out, B);
  not not_120 (not_120_out, C);
  not not_121 (not_121_out, B);
  not not_122 (not_122_out, D);
  not not_123 (not_123_out, C);
  not not_124 (not_124_out, D);
  not not_125 (not_125_out, A);
  not not_126 (not_126_out, B);
  not not_127 (not_127_out, A);
  not not_128 (not_128_out, C);
  not not_129 (not_129_out, A);
  not not_130 (not_130_out, D);
  not not_131 (not_131_out, B);
  not not_132 (not_132_out, C);
  not not_133 (not_133_out, B);
  not not_134 (not_134_out, D);
  not not_135 (not_135_out, C);
  not not_136 (not_136_out, D);
  not not_137 (not_137_out, A);
  not not_138 (not_138_out, B);
  not not_139 (not_139_out, C);
  not not_140 (not_140_out, D);
  and and_1 (and_1_out, not_1_out, not_2_out, not_3_out, not_4_out, H);
  and and_2 (and_2_out, not_5_out, not_6_out, not_7_out, not_8_out, G);
  and and_3 (and_3_out, not_9_out, not_10_out, not_11_out, G, H);
  and and_4 (and_4_out, not_12_out, not_13_out, not_14_out, G, H);
  and and_5 (and_5_out, not_15_out, not_16_out, not_17_out, G, H);
  and and_6 (and_6_out, not_18_out, not_19_out, not_20_out, G, H);
  and and_7 (and_7_out, not_21_out, not_22_out, not_23_out, not_24_out, F);
  and and_8 (and_8_out, not_25_out, not_26_out, not_27_out, F, H);
  and and_9 (and_9_out, not_28_out, not_29_out, not_30_out, F, H);
  and and_10 (and_10_out, not_31_out, not_32_out, not_33_out, F, H);
  and and_11 (and_11_out, not_34_out, not_35_out, not_36_out, F, H);
  and and_12 (and_12_out, not_37_out, not_38_out, not_39_out, F, G);
  and and_13 (and_13_out, not_40_out, not_41_out, not_42_out, F, G);
  and and_14 (and_14_out, not_43_out, not_44_out, not_45_out, F, G);
  and and_15 (and_15_out, not_46_out, not_47_out, not_48_out, F, G);
  and and_16 (and_16_out, not_49_out, not_50_out, F, G, H);
  and and_17 (and_17_out, not_51_out, not_52_out, F, G, H);
  and and_18 (and_18_out, not_53_out, not_54_out, F, G, H);
  and and_19 (and_19_out, not_55_out, not_56_out, F, G, H);
  and and_20 (and_20_out, not_57_out, not_58_out, F, G, H);
  and and_21 (and_21_out, not_59_out, not_60_out, F, G, H);
  and and_22 (and_22_out, not_61_out, not_62_out, not_63_out, not_64_out, E);
  and and_23 (and_23_out, not_65_out, not_66_out, not_67_out, E, H);
  and and_24 (and_24_out, not_68_out, not_69_out, not_70_out, E, H);
  and and_25 (and_25_out, not_71_out, not_72_out, not_73_out, E, H);
  and and_26 (and_26_out, not_74_out, not_75_out, not_76_out, E, H);
  and and_27 (and_27_out, not_77_out, not_78_out, not_79_out, E, G);
  and and_28 (and_28_out, not_80_out, not_81_out, not_82_out, E, G);
  and and_29 (and_29_out, not_83_out, not_84_out, not_85_out, E, G);
  and and_30 (and_30_out, not_86_out, not_87_out, not_88_out, E, G);
  and and_31 (and_31_out, not_89_out, not_90_out, E, G, H);
  and and_32 (and_32_out, not_91_out, not_92_out, E, G, H);
  and and_33 (and_33_out, not_93_out, not_94_out, E, G, H);
  and and_34 (and_34_out, not_95_out, not_96_out, E, G, H);
  and and_35 (and_35_out, not_97_out, not_98_out, E, G, H);
  and and_36 (and_36_out, not_99_out, not_100_out, E, G, H);
  and and_37 (and_37_out, not_101_out, not_102_out, not_103_out, E, F);
  and and_38 (and_38_out, not_104_out, not_105_out, not_106_out, E, F);
  and and_39 (and_39_out, not_107_out, not_108_out, not_109_out, E, F);
  and and_40 (and_40_out, not_110_out, not_111_out, not_112_out, E, F);
  and and_41 (and_41_out, not_113_out, not_114_out, E, F, H);
  and and_42 (and_42_out, not_115_out, not_116_out, E, F, H);
  and and_43 (and_43_out, not_117_out, not_118_out, E, F, H);
  and and_44 (and_44_out, not_119_out, not_120_out, E, F, H);
  and and_45 (and_45_out, not_121_out, not_122_out, E, F, H);
  and and_46 (and_46_out, not_123_out, not_124_out, E, F, H);
  and and_47 (and_47_out, not_125_out, not_126_out, E, F, G);
  and and_48 (and_48_out, not_127_out, not_128_out, E, F, G);
  and and_49 (and_49_out, not_129_out, not_130_out, E, F, G);
  and and_50 (and_50_out, not_131_out, not_132_out, E, F, G);
  and and_51 (and_51_out, not_133_out, not_134_out, E, F, G);
  and and_52 (and_52_out, not_135_out, not_136_out, E, F, G);
  and and_53 (and_53_out, not_137_out, E, F, G, H);
  and and_54 (and_54_out, not_138_out, E, F, G, H);
  and and_55 (and_55_out, not_139_out, E, F, G, H);
  and and_56 (and_56_out, not_140_out, E, F, G, H);
  or or_1 (or_1_out, and_1_out, and_2_out, and_3_out, and_4_out, and_5_out, and_6_out, and_7_out, and_8_out, and_9_out, and_10_out, and_11_out, and_12_out, and_13_out, and_14_out, and_15_out, and_16_out, and_17_out, and_18_out, and_19_out, and_20_out, and_21_out, and_22_out, and_23_out, and_24_out, and_25_out, and_26_out, and_27_out, and_28_out);
  or or_2 (or_2_out, and_29_out, and_30_out, and_31_out, and_32_out, and_33_out, and_34_out, and_35_out, and_36_out, and_37_out, and_38_out, and_39_out, and_40_out, and_41_out, and_42_out, and_43_out, and_44_out, and_45_out, and_46_out, and_47_out, and_48_out, and_49_out, and_50_out, and_51_out, and_52_out, and_53_out, and_54_out, and_55_out, and_56_out);
  or or_3 (x, or_1_out, or_2_out);
endmodule

module _7_hex (
  input  A,
  input  B,
  input  C,
  input  D,
  output a_2,
  output b_2,
  output c_2,
  output d_2,
  output e,
  output f,
  output g
);

  wire and_1_out, and_2_out, and_3_out, and_4_out, and_5_out, and_6_out, and_7_out, and_8_out, and_9_out,
       and_10_out, and_11_out, and_12_out, and_13_out, and_14_out, and_15_out, and_16_out, not_1_out,
       not_2_out, not_3_out, not_4_out, not_5_out, not_6_out, not_7_out, not_8_out, not_9_out, not_10_out,
       not_11_out, not_12_out, not_13_out, not_14_out, not_15_out, not_16_out, not_17_out, not_18_out,
       not_19_out, not_20_out, not_21_out;

  not not_1 (not_1_out, B);
  and and_1 (and_1_out, not_1_out, not_2_out);
  not not_2 (not_2_out, D);
  and and_2 (and_2_out, B, D);
  not not_3 (not_3_out, B);
  not not_4 (not_4_out, C);
  and and_3 (and_3_out, not_4_out, not_5_out);
  not not_5 (not_5_out, D);
  and and_4 (and_4_out, C, D);
  not not_6 (not_6_out, C);
  or or_1 (c_2, not_6_out, D, B);
  not not_7 (not_7_out, B);
  and and_5 (and_5_out, not_7_out, not_8_out);
  not not_8 (not_8_out, D);
  not not_9 (not_9_out, B);
  and and_6 (and_6_out, not_9_out, C);
  and and_7 (and_7_out, C, not_10_out);
  not not_10 (not_10_out, D);
  not not_11 (not_11_out, C);
  and and_8 (and_8_out, B, not_11_out, D);
  not not_12 (not_12_out, B);
  and and_9 (and_9_out, not_12_out, not_13_out);
  not not_13 (not_13_out, D);
  and and_10 (and_10_out, C, not_14_out);
  not not_14 (not_14_out, D);
  not not_15 (not_15_out, C);
  and and_11 (and_11_out, not_15_out, not_16_out);
  not not_16 (not_16_out, D);
  and and_12 (and_12_out, B, not_17_out);
  not not_17 (not_17_out, C);
  and and_13 (and_13_out, B, not_18_out);
  not not_18 (not_18_out, D);
  not not_19 (not_19_out, B);
  and and_14 (and_14_out, not_19_out, C);
  and and_15 (and_15_out, B, not_20_out);
  not not_20 (not_20_out, C);
  and and_16 (and_16_out, B, not_21_out);
  not not_21 (not_21_out, D);
  or or_2 (a_2, and_1_out, C, and_2_out, A);
  or or_3 (b_2, not_3_out, and_3_out, and_4_out);
  or or_4 (d_2, and_5_out, and_6_out, and_7_out, and_8_out, A);
  or or_5 (e, and_9_out, and_10_out);
  or or_6 (f, and_11_out, and_12_out, and_13_out, A);
  or or_7 (g, and_14_out, and_15_out, and_16_out, A);
endmodule
