// Logisim project parcial3.circ as structural Verilog: 5 circuits, main circuit contador
module main (
  input  in_1,
  input  in_2,
  input  in_3,
  input  in_4,
  input  in_5,
  input  in_6,
  input  in_7,
  input  in_8
);

  wire comparar_1_out_9, comparar_1_out_10, contador_1_a_2, contador_1_b_2, contador_1_c_2, contador_2_a_2,
       contador_2_b_2, contador_2_c_2, relo_1_n_2, relo_1_o_2, relo_1_out_3, relo_1_out_4, relo_1_out_5,
       relo_1_out_6, relo_1_out_7, relo_1_out_8;
  wire [2:0] n7_hex_1_out_6, n7_hex_2_out_6, n7_hex_3_out_6, n7_hex_4_out_6, n7_hex_5_out_6, n7_hex_6_out_6;
  wire [3:0] n7_hex_1_out_5, n7_hex_2_out_5, n7_hex_3_out_5, n7_hex_4_out_5, n7_hex_5_out_5, n7_hex_6_out_5;

  comparar comparar_1 (
    .A(in_1), .B(in_2), .C(in_3), .D(in_4), .E(in_5), .F(in_6), .G(in_7), .H(in_8), .out_9(comparar_1_out_9),
    .out_10(comparar_1_out_10));
  _7_hex u_7_hex_1 (
    .A(1'b0), .B(contador_1_a_2), .C(contador_1_b_2), .D(contador_1_c_2), .out_5(n7_hex_1_out_5),
    .out_6(n7_hex_1_out_6));
  contador contador_1 (
    .A(in_1), .B(in_2), .C(in_3), .D(in_4), .a_2(contador_1_a_2), .b_2(contador_1_b_2), .c_2(contador_1_c_2));
  contador contador_2 (
    .A(in_5), .B(in_6), .C(in_7), .D(in_8), .a_2(contador_2_a_2), .b_2(contador_2_b_2), .c_2(contador_2_c_2));
  _7_hex u_7_hex_2 (
    .A(1'b0), .B(contador_2_a_2), .C(contador_2_b_2), .D(contador_2_c_2), .out_5(n7_hex_2_out_5),
    .out_6(n7_hex_2_out_6));
  relo relo_1 (
    .N(comparar_1_out_9), .O(comparar_1_out_10), .out_3(relo_1_out_3), .out_4(relo_1_out_4),
    .out_5(relo_1_out_5), .out_6(relo_1_out_6), .out_7(relo_1_out_7), .out_8(relo_1_out_8), .O_2(relo_1_o_2),
    .N_2(relo_1_n_2));
  _7_Segment_Display u_7_segment_display_1 (
    .g(n7_hex_1_out_5[3]), .f(n7_hex_1_out_5[2]), .a(n7_hex_1_out_5[1]), .b(n7_hex_1_out_5[0]),
    .e(n7_hex_1_out_6[2]), .d(n7_hex_1_out_6[1]), .c(n7_hex_1_out_6[0]));  // open: dp
  _7_Segment_Display u_7_segment_display_2 (
    .g(n7_hex_2_out_5[3]), .f(n7_hex_2_out_5[2]), .a(n7_hex_2_out_5[1]), .b(n7_hex_2_out_5[0]),
    .e(n7_hex_2_out_6[2]), .d(n7_hex_2_out_6[1]), .c(n7_hex_2_out_6[0]));  // open: dp
  LED E (.in(relo_1_o_2));
  LED E_2 (.in(relo_1_o_2));
  _7_Segment_Display u_7_segment_display_3 (
    .g(n7_hex_3_out_5[3]), .f(n7_hex_3_out_5[2]), .a(n7_hex_3_out_5[1]), .b(n7_hex_3_out_5[0]),
    .e(n7_hex_3_out_6[2]), .d(n7_hex_3_out_6[1]), .c(n7_hex_3_out_6[0]));  // open: dp
  _7_hex u_7_hex_3 (
    .A(1'b0), .B(1'b0), .C(relo_1_out_7), .D(relo_1_out_8), .out_5(n7_hex_3_out_5), .out_6(n7_hex_3_out_6));
  _7_Segment_Display u_7_segment_display_4 (
    .g(n7_hex_4_out_5[3]), .f(n7_hex_4_out_5[2]), .a(n7_hex_4_out_5[1]), .b(n7_hex_4_out_5[0]),
    .e(n7_hex_4_out_6[2]), .d(n7_hex_4_out_6[1]), .c(n7_hex_4_out_6[0]));  // open: dp
  _7_hex u_7_hex_4 (
    .A(1'b0), .B(1'b0), .C(relo_1_out_7), .D(relo_1_out_8), .out_5(n7_hex_4_out_5), .out_6(n7_hex_4_out_6));
  LED O (.in(relo_1_o_2));
  LED N (.in(relo_1_n_2));
  LED O_2 (.in(relo_1_o_2));
  LED N_2 (.in(relo_1_n_2));
  _7_Segment_Display u_7_segment_display_5 (
    .g(n7_hex_5_out_5[3]), .f(n7_hex_5_out_5[2]), .a(n7_hex_5_out_5[1]), .b(n7_hex_5_out_5[0]),
    .e(n7_hex_5_out_6[2]), .d(n7_hex_5_out_6[1]), .c(n7_hex_5_out_6[0]));  // open: dp
  _7_hex u_7_hex_5 (
    .A(relo_1_out_3), .B(relo_1_out_4), .C(relo_1_out_5), .D(relo_1_out_6), .out_5(n7_hex_5_out_5),
    .out_6(n7_hex_5_out_6));
  _7_Segment_Display u_7_segment_display_6 (
    .g(n7_hex_6_out_5[3]), .f(n7_hex_6_out_5[2]), .a(n7_hex_6_out_5[1]), .b(n7_hex_6_out_5[0]),
    .e(n7_hex_6_out_6[2]), .d(n7_hex_6_out_6[1]), .c(n7_hex_6_out_6[0]));  // open: dp
  _7_hex u_7_hex_6 (
    .A(relo_1_out_3), .B(relo_1_out_4), .C(relo_1_out_5), .D(relo_1_out_6), .out_5(n7_hex_6_out_5),
    .out_6(n7_hex_6_out_6));
  LED S (.in(relo_1_n_2));
  LED S_2 (.in(relo_1_n_2));
endmodule

module contador (
  input  A,
  input  B,
  input  C,
  input  D,
  output a_2,
  output b_2,
  output c_2
);

  wire and_2_out, and_3_out, and_4_out, and_5_out, and_6_out, and_7_out, and_8_out, and_9_out, and_10_out,
       and_11_out, and_12_out, and_13_out, and_14_out, and_15_out, and_16_out, not_1_out, not_2_out,
       not_3_out, not_4_out, not_5_out, not_6_out, not_7_out, not_8_out, not_9_out, not_10_out, not_11_out,
       not_12_out, not_13_out, not_14_out, not_15_out, not_16_out, not_17_out, not_18_out, not_19_out,
       not_20_out, not_21_out, not_22_out, not_23_out;

  and and_1 (a_2, A, B, C, D);
  not not_1 (not_1_out, A);
  and and_2 (and_2_out, not_1_out, C, D);
  not not_2 (not_2_out, A);
  and and_3 (and_3_out, not_2_out, B, D);
  not not_3 (not_3_out, A);
  and and_4 (and_4_out, not_3_out, B, C);
  and and_5 (and_5_out, A, not_4_out, D);
  not not_4 (not_4_out, B);
  and and_6 (and_6_out, A, not_5_out, C);
  not not_5 (not_5_out, B);
  and and_7 (and_7_out, A, B, not_6_out);
  not not_6 (not_6_out, C);
  and and_8 (and_8_out, A, B, not_7_out);
  not not_7 (not_7_out, D);
  not not_8 (not_8_out, A);
  not not_9 (not_9_out, B);
  not not_10 (not_10_out, C);
  not not_11 (not_11_out, A);
  not not_12 (not_12_out, B);
  not not_13 (not_13_out, D);
  not not_14 (not_14_out, A);
  not not_15 (not_15_out, C);
  not not_16 (not_16_out, D);
  not not_17 (not_17_out, A);
  not not_18 (not_18_out, B);
  not not_19 (not_19_out, C);
  not not_20 (not_20_out, D);
  not not_21 (not_21_out, B);
  not not_22 (not_22_out, C);
  not not_23 (not_23_out, D);
  and and_9 (and_9_out, not_8_out, not_9_out, not_10_out, D);
  and and_10 (and_10_out, not_11_out, not_12_out, C, not_13_out);
  and and_11 (and_11_out, not_14_out, B, not_15_out, not_16_out);
  and and_12 (and_12_out, not_17_out, B, C, D);
  and and_13 (and_13_out, A, not_18_out, not_19_out, not_20_out);
  and and_14 (and_14_out, A, not_21_out, C, D);
  and and_15 (and_15_out, A, B, not_22_out, D);
  and and_16 (and_16_out, A, B, C, not_23_out);
  or or_1 (b_2, and_2_out, and_3_out, and_4_out, and_5_out, and_6_out, and_7_out, and_8_out);
  or or_2 (c_2, and_9_out, and_10_out, and_11_out, and_12_out, and_13_out, and_14_out, and_15_out, and_16_out);
endmodule

module comparar (
  input  A,
  input  B,
  input  C,
  input  D,
  input  E,
  input  F,
  input  G,
  input  H,
  output out_9,
  output out_10
);

  wire comparator_1_gt;
  wire [2:0] and_1_out, and_2_out, bitadder_1_out, bitadder_2_out;
  wire [2:1] and_3_out;

  BitAdder #(.width(4)) bitadder_1 (.in0({D, C, B, A}), .out(bitadder_1_out));
  BitAdder #(.width(4)) bitadder_2 (.in0({H, G, F, E}), .out(bitadder_2_out));
  assign and_1_out = 3'b100 & bitadder_1_out;  // AND_Gate and_1, 3 bits wide
  assign and_2_out = 3'b100 & bitadder_2_out;  // AND_Gate and_2, 3 bits wide
  Comparator #(.width(3), .mode("unsigned")) comparator_1 (
    .a(and_1_out), .b(and_2_out), .gt(comparator_1_gt), .lt(out_10));  // open: eq
  assign {and_3_out, and_3_out[1]} = bitadder_1_out & bitadder_2_out & 3'b100;  // AND_Gate and_3, 3 bits wide
  or or_1 (out_9, comparator_1_gt, and_3_out[2]);
  // also tied to GND on the sheet: and_3_out[1]
endmodule

module _7_hex (
  input  A,
  input  B,
  input  C,
  input  D,
  output [3:0] out_5,
  output [2:0] out_6
);

  wire and_1_out, and_2_out, and_3_out, and_4_out, and_5_out, and_6_out, and_7_out, and_8_out, and_9_out,
       and_10_out, and_11_out, and_12_out, and_13_out, and_14_out, and_15_out, and_16_out, not_1_out,
       not_2_out, not_3_out, not_4_out, not_5_out, not_6_out, not_7_out, not_8_out, not_9_out, not_10_out,
       not_11_out, not_12_out, not_13_out, not_14_out, not_15_out, not_16_out, not_17_out, not_18_out,
       not_19_out, not_20_out, not_21_out;

  not not_1 (not_1_out, B);
  and and_1 (and_1_out, not_1_out, not_2_out);
  not not_2 (not_2_out, D);
  and and_2 (and_2_out, B, D);
  not not_3 (not_3_out, B);
  not not_4 (not_4_out, C);
  and and_3 (and_3_out, not_4_out, not_5_out);
  not not_5 (not_5_out, D);
  and and_4 (and_4_out, C, D);
  not not_6 (not_6_out, C);
  or or_1 (out_6[0], not_6_out, D, B);
  not not_7 (not_7_out, B);
  and and_5 (and_5_out, not_7_out, not_8_out);
  not not_8 (not_8_out, D);
  not not_9 (not_9_out, B);
  and and_6 (and_6_out, not_9_out, C);
  and and_7 (and_7_out, C, not_10_out);
  not not_10 (not_10_out, D);
  and and_8 (and_8_out, B, not_11_out, D);
  not not_11 (not_11_out, C);
  not not_12 (not_12_out, B);
  and and_9 (and_9_out, not_12_out, not_13_out);
  not not_13 (not_13_out, D);
  and and_10 (and_10_out, C, not_14_out);
  not not_14 (not_14_out, D);
  not not_15 (not_15_out, C);
  and and_11 (and_11_out, not_15_out, not_16_out);
  not not_16 (not_16_out, D);
  and and_12 (and_12_out, B, not_17_out);
  not not_17 (not_17_out, C);
  and and_13 (and_13_out, B, not_18_out);
  not not_18 (not_18_out, D);
  not not_19 (not_19_out, B);
  and and_14 (and_14_out, not_19_out, C);
  and and_15 (and_15_out, B, not_20_out);
  not not_20 (not_20_out, C);
  and and_16 (and_16_out, B, not_21_out);
  not not_21 (not_21_out, D);
  or or_2 (out_5[1], and_1_out, C, and_2_out, A);
  or or_3 (out_5[0], not_3_out, and_3_out, and_4_out);
  or or_4 (out_6[1], and_5_out, and_6_out, and_7_out, and_8_out, A);
  or or_5 (out_6[2], and_9_out, and_10_out);
  or or_6 (out_5[2], and_11_out, and_12_out, and_13_out, A);
  or or_7 (out_5[3], and_14_out, and_15_out, and_16_out, A);
endmodule

module relo (
  input  N,
  input  O,
  output out_3,
  output out_4,
  output out_5,
  output out_6,
  output out_7,
  output out_8,
  output O_2,
  output N_2
);

  wire and_1_out, clock_1_out, j_k_ff_1_qn, j_k_ff_2_qn, j_k_ff_3_qn, j_k_ff_4_qn, or_1_out;
  wire [4:0] j_k_ff_1_q, subtractor_1_out;
  wire [4:4] divider_1_out, divider_1_rem;

  and and_1 (and_1_out, j_k_ff_1_q[4], j_k_ff_1_q[2], j_k_ff_1_q[0]);
  Clock clock_1 (.out(clock_1_out));
  J_K_Flip_Flop j_k_ff_1 (
    .J(1'b1), .clk(clock_1_out), .K(1'b1), .Q(j_k_ff_1_q[0]), .Qn(j_k_ff_1_qn), .en(1'b1), .reset(and_1_out));  // open: preset
  J_K_Flip_Flop j_k_ff_2 (
    .J(1'b1), .clk(j_k_ff_1_qn), .K(1'b1), .Q(j_k_ff_1_q[1]), .Qn(j_k_ff_2_qn), .en(1'b1), .reset(and_1_out));  // open: preset
  J_K_Flip_Flop j_k_ff_3 (
    .J(1'b1), .clk(j_k_ff_2_qn), .K(1'b1), .Q(j_k_ff_1_q[2]), .Qn(j_k_ff_3_qn), .preset(or_1_out), .en(1'b1),
    .reset(and_1_out));
  J_K_Flip_Flop j_k_ff_4 (
    .J(1'b1), .clk(j_k_ff_3_qn), .K(1'b1), .Q(j_k_ff_1_q[3]), .Qn(j_k_ff_4_qn), .en(1'b1), .reset(and_1_out));  // open: preset
  or or_1 (or_1_out, N, O);
  J_K_Flip_Flop j_k_ff_5 (
    .J(1'b1), .clk(j_k_ff_4_qn), .K(1'b1), .Q(j_k_ff_1_q[4]), .preset(or_1_out), .en(1'b1), .reset(and_1_out));  // open: Qn
  Subtractor #(.width(5)) subtractor_1 (.a(5'b10100), .b(j_k_ff_1_q), .out(subtractor_1_out));  // open: bin, bout
  J_K_Flip_Flop j_k_ff_6 (.J(1'b1), .clk(and_1_out), .K(1'b1), .Q(O_2), .Qn(N_2), .preset(O), .en(1'b1), .reset(N));
  Divider #(.width(5)) divider_1 (
    .a(subtractor_1_out), .b(5'b01010), .out({{3{divider_1_out[4]}}, out_7, out_8}),
    .rem({divider_1_rem[4], out_3, out_4, out_5, out_6}));  // open: upper
  // also tied to GND on the sheet: {divider_1_rem[4], divider_1_out[4]}
endmodule
