// Logisim project PARCIAL_2.circ as structural Verilog: 1 circuit, main circuit main
module main (
  input  A,
  input  A_2,
  input  B,
  input  B_2,
  input  C,
  input  C_2,
  input  D,
  input  D_2,
  input  A1,
  input  A2,
  input  B1,
  input  B2,
  output out_13,
  output out_14,
  output out_15,
  output out_16,
  output out_17,
  output out_18,
  output out_19,
  output out_20
);

  wire and_3_out, and_4_out, and_5_out, and_6_out, and_7_out, and_8_out, and_9_out, and_10_out, not_1_out,
       not_2_out, not_3_out, not_4_out, not_5_out, not_6_out, not_7_out, not_8_out, not_9_out, not_10_out,
       not_11_out, not_12_out, or_1_out, or_2_out, or_3_out, or_4_out, xnor_1_out, xnor_2_out;

  and and_1 (out_13, A, A_2, B, B_2);
  not not_1 (not_1_out, A);
  not not_2 (not_2_out, A_2);
  not not_3 (not_3_out, B);
  not not_4 (not_4_out, B_2);
  not not_5 (not_5_out, C);
  not not_6 (not_6_out, C_2);
  not not_7 (not_7_out, D);
  not not_8 (not_8_out, D_2);
  or or_1 (or_1_out, A, A_2);
  or or_2 (or_2_out, B, B_2);
  or or_3 (or_3_out, C, C_2);
  or or_4 (or_4_out, D, D_2);
  and and_2 (out_14, not_1_out, not_2_out, not_3_out, not_4_out, not_5_out, not_6_out, not_7_out, not_8_out);
  and and_3 (and_3_out, or_1_out, xnor_1_out);
  xnor xnor_1 (xnor_1_out, or_2_out, or_3_out);
  and and_4 (and_4_out, xnor_1_out, or_4_out);
  xnor xnor_2 (xnor_2_out, A2, B1);
  not not_9 (not_9_out, or_3_out);
  and and_5 (and_5_out, not_9_out, or_2_out);
  not not_10 (not_10_out, or_2_out);
  and and_6 (and_6_out, not_10_out, or_3_out);
  and and_7 (and_7_out, A1, xnor_2_out);
  not not_11 (not_11_out, B1);
  and and_8 (and_8_out, not_11_out, A2);
  not not_12 (not_12_out, A2);
  and and_9 (and_9_out, not_12_out, B1);
  and and_10 (and_10_out, xnor_2_out, B2);
  or or_5 (out_15, and_3_out, and_5_out);
  or or_6 (out_17, and_6_out, and_4_out);
  or or_7 (out_18, and_7_out, and_8_out);
  or or_8 (out_20, and_9_out, and_10_out);
  xnor xnor_3 (out_16, out_15, out_17);
  xnor xnor_4 (out_19, out_18, out_20);
endmodule
